# Fritzing sketch alarmmobil (saved by Fritzing 0.9.3b)

parts:
  Part1 = Arduino Uno (Rev3)
  S1 = Round Pushbutton
  VCC1 = Battery block 9V
  Part2 = Gas Sensor Breakout Board
  S2 = KY-026
  R2 = Resistor [tolerance=±5% resistance=4.7k package=THT]
  R3 = Resistor [tolerance=±5% resistance=4.7k package=THT]
  U2 = Mini-360 DC-DC Buck converter [package=THT]
  GSM_SIM_GPSR_SMS_SIM900_SIM1 = SIM800L [package=THT]

nets:
  N1: Part1.D10_PWM/SS, GSM_SIM_GPSR_SMS_SIM900_SIM1.SIM_TXD
  N2: Part1.D11_PWM/MOSI, GSM_SIM_GPSR_SMS_SIM900_SIM1.SIM_RXD
  N3: Part1.D3_PWM, Part2.H1
  N4: Part1.D4, S1.leg0, R3.Pin_1
  N5: Part1.D5_PWM, S2.pin4
  N6: Part1.5V, Part2.A1, S2.pin3
  N7: S1.leg1, Part2.GND, S2.pin2, GSM_SIM_GPSR_SMS_SIM900_SIM1.GND#5
  N8: VCC1.-, U2.IN-
  N9: VCC1.+, U2.IN+
  N10: R2.Pin_1, R3.Pin_0
  N11: U2.OUT+, GSM_SIM_GPSR_SMS_SIM900_SIM1.VDD
  N12: U2.OUT-, GSM_SIM_GPSR_SMS_SIM900_SIM1.GND#1

custom parts:
  KY-026: ky-026 flame sensor module
  Mini-360 DC-DC Buck converter: Mini-360 DC-DC Buck converter. Tiny buck step down voltage converter, input voltage 4.75 to 23V output 1 to 17V adjustable. Available from ebay and the like.
